// Logisim project Ctl_Load_Store.circ as structural Verilog: 1 circuit, main circuit Load_Store
module Load_Store (
  input  Clk,
  input  Enable,
  input  Reset,
  input  [15:0] Instruction,
  input  [31:0] Stack_Pointer,
  output Store,
  output Load,
  output PC_Hold,
  output [31:0] RAM_Addr,
  output [2:0] Rmd
);

  wire and_1_out, d_ff_1_q, d_ff_1_qn, not_1_out, or_1_out;
  wire [31:0] adder_1_out, bit_extender_1_out, bit_extender_2_out;

  Multiplexer #(.width(3)) multiplexer_1 (.in0(3'b000), .in1(Instruction[10:8]), .out(Rmd), .sel(Enable));
  assign bit_extender_1_out = {{24{1'b0}}, Instruction[7:0]};  // Bit_Extender bit_extender_1
  D_Flip_Flop #(.trigger("falling")) d_ff_1 (
    .D(and_1_out), .clk(Clk), .Q(d_ff_1_q), .Qn(d_ff_1_qn), .reset(or_1_out));  // open: preset
  and and_1 (and_1_out, d_ff_1_qn, Instruction[11]);
  or or_1 (or_1_out, ~Enable, Reset, ~Instruction[11]);  // OR_Gate
  not not_1 (not_1_out, Instruction[11]);
  assign bit_extender_2_out = {{31{1'b1}}, Enable};  // Bit_Extender bit_extender_2
  Adder #(.width(32)) adder_1 (.a(bit_extender_1_out), .b(Stack_Pointer), .out(adder_1_out));  // open: cin, cout
  and and_2 (Store, Enable, not_1_out);
  and and_3 (Load, Enable, d_ff_1_q, Instruction[11]);
  and and_4 (PC_Hold, d_ff_1_qn, Enable, Instruction[11]);
  assign RAM_Addr = bit_extender_2_out & adder_1_out;  // AND_Gate and_5, 32 bits wide

  // Other names for the same wires on the sheet: Clock = Clk; E = Enable; RM[2:0] = Instruction[10:8];
  //   Bit11 = Instruction[11]; R = Reset

  // Notes on the sheet:
  //   Delay load and hold PC for 1 cycle for the RAM to send out requested data 
endmodule
